// Logisim project LC3-1-0.circ as structural Verilog: 13 circuits, main circuit main
module main (
  input  RESET
);

  wire ADDR1M, Clock, CLOCK_out, d_ff_1_q, GALU, GetChar, GMDR, GMRMX, GO, GPC, GPC_1, GPSR, GSP, immS, KBSR,
       Load_Disp, MARM, MIO_EN, multiplexer_1_out, not_1_out, or_1_out, priorety_int_1_int;
  wire [1:0] ADDR2M, ALUKM, DRM;
  wire [2:0] DR, NZP, SR1, SR2, undriven;
  wire [6:0] Display, KBDR;
  wire [15:0] BUS, memoryio_1_gatemdr, pcir_1_gatemarmux, pcir_1_gatepc, pcir_1_immout, pcir_1_to_fsmc,
       pu_1_alu_to_bus, sp_logic_1_gatesp, SR1OUT, subtractor_1_out, vector_1_gatevector;
  wire [19:0] MUX;
  wire [19:3] GTS;

  Clock u_CLOCK (.out(CLOCK_out));
  and and_1 (Clock, CLOCK_out, GO);
  or or_1 (or_1_out, RESET, GTS[11]);
  Multiplexer #(.enable("false")) multiplexer_1 (.in0(not_1_out), .in1(BUS[15]), .out(multiplexer_1_out), .sel(MUX[5]));
  not not_1 (not_1_out, MUX[0]);
  assign BUS = GMRMX ? pcir_1_gatemarmux : 16'bz;  // Controlled_Buffer controlled_buffer_1
  PCIR pcir_1 (
    .LD_PC(GTS[12]), .FINITE_TO_PCMUX(MUX[19:18]), .ADDR2MUX(ADDR2M), .LD_IR(GTS[16]), .Clk(Clock),
    .SR1_IN(SR1OUT), .immOUT(pcir_1_immout), .TO_FSMC(pcir_1_to_fsmc), .BUS_TO_PCMUX(BUS),
    .GatePC(pcir_1_gatepc), .BUS_IN(BUS), .MARMUX(MARM), .GateMARMUX(pcir_1_gatemarmux), .ADDR1MUX(ADDR1M),
    .RESET(RESET));
  D_Flip_Flop #(.trigger("falling")) d_ff_1 (
    .clk(Clock), .D(multiplexer_1_out), .Q(d_ff_1_q), .preset(RESET), .en(or_1_out));  // open: Qn, reset
  assign BUS[15] = GPSR ? d_ff_1_q : 1'bz;  // Controlled_Buffer controlled_buffer_2
  MEMORYIO memoryio_1 (
    .LD_MAR(GTS[18]), .LD_MDR(GTS[17]), .Clk(Clock), .GateMDR(memoryio_1_gatemdr), .reset(RESET), .BUS(BUS),
    .MIO_EN(MIO_EN), .R_W(MUX[1]), .GOOUT(GO), .ASCII_OUT(Display), .LD_DDR(Load_Disp), .GetChar(GetChar),
    .KBSR(KBSR), .KBDR(KBDR));
  Subtractor #(.width(16)) subtractor_1 (.a(pcir_1_gatepc), .b(16'h1), .out(subtractor_1_out));  // open: bin, bout
  assign BUS = GPC ? pcir_1_gatepc : 16'bz;  // Controlled_Buffer controlled_buffer_3
  FSM FSM (
    .R(1'b1), .PSR_15(d_ff_1_q), .INT(priorety_int_1_int), .IR(pcir_1_to_fsmc), .NZP(NZP), .Clk(Clock),
    .immSelect(immS), .RESET(RESET),
    .LD_GATE_OUT({GTS[19:8], GPC, GMDR, GALU, GMRMX, GTS[3], GPC_1, GPSR, GSP}),
    .MUX_and_misc({MUX[19:18], DRM, MUX[15:14], ADDR1M, ADDR2M, MUX[10:9], MARM, MUX[7:5], ALUKM, MIO_EN, MUX[1:0]}),
    .DR_Select(DR), .SR1_Select(SR1), .SR2_Select(SR2));
  NZP_LOGIC nzp_logic_1 (
    .PSRMUX(MUX[5]), .NZP_OUT(NZP), .NZP_LOGIC_IN(BUS), .PSR_2_0(BUS[2:0]), .LD_CC(GTS[13]), .Clk(Clock));
  assign BUS = GMDR ? memoryio_1_gatemdr : 16'bz;  // Controlled_Buffer controlled_buffer_4
  assign BUS[2:0] = GPSR ? NZP : 3'bz;  // Controlled_Buffer controlled_buffer_5
  assign BUS = GPC_1 ? subtractor_1_out : 16'bz;  // Controlled_Buffer controlled_buffer_6
  PU pu_1 (
    .DR(DR), .LD_REG(GTS[14]), .SR2(SR2), .immeSelect(immS), .ALUK(ALUKM), .SR1(SR1),
    .immeSEXT(pcir_1_immout), .BUS_IN(BUS), .Clk(Clock), .ALU_TO_BUS(pu_1_alu_to_bus), .SR1OUT(SR1OUT),
    .RESET(RESET));
  assign BUS = GALU ? pu_1_alu_to_bus : 16'bz;  // Controlled_Buffer controlled_buffer_7
  Priorety_INT priorety_int_1 (
    .LD_Priv(GTS[11]), .PSRMux(MUX[5]), .Clk(Clock), .BUS_10_8(BUS[10:8]), .To_BUS__10_8(undriven),
    .INT(priorety_int_1_int));
  assign BUS[10:8] = GPSR ? undriven : 3'bz;  // Controlled_Buffer controlled_buffer_8
  SP_logic sp_logic_1 (
    .SPMUX(MUX[10:9]), .LD_SavedUSP(GTS[9]), .LD_SavedSSP(GTS[10]), .GateSP(sp_logic_1_gatesp), .SR1IN(SR1OUT));
  assign BUS = GPSR ? sp_logic_1_gatesp : 16'bz;  // Controlled_Buffer controlled_buffer_9
  assign BUS = GTS[3] ? vector_1_gatevector : 16'bz;  // Controlled_Buffer controlled_buffer_10
  Vector vector_1 (.GateVector(vector_1_gatevector), .INTV({8{1'b0}}), .VectorMUX(MUX[7:6]));
  TTY #(.rows(30), .cols(80)) tty_1 (.data(Display), .clk(Clock), .we(Load_Disp), .clr(RESET));
  Keyboard keyboard_1 (.clk(Clock), .re(GetChar), .clr(RESET), .avail(KBSR), .data(KBDR));

  // Other names for the same wires on the sheet: GTS (some bits) = {GPC, GMDR, GALU, GMRMX, GPC_1, GPSR, GSP};
  //   GVect = GTS[3]; LVect = GTS[8]; LSUSP = GTS[9]; LSSSP = GTS[10]; LPriv = GTS[11]; LPC = GTS[12]; LCC = GTS[13];
  //   LREG = GTS[14]; LBEN = GTS[15]; LIR = GTS[16]; LMDR = GTS[17]; LMAR = GTS[18]; LPrio = GTS[19];
  //   Set_Priv = MUX[0]; R_W = MUX[1]; MUX (some bits) = {DRM, ADDR1M, ADDR2M, MARM, ALUKM, MIO_EN}; PRSM = MUX[5];
  //   VectM[1:0] = MUX[7:6]; SPM[1:0] = MUX[10:9]; SR1M[1:0] = MUX[15:14]; PCM[1:0] = MUX[19:18]

  // Notes on the sheet:
  //   Load programs here->
  //   Keyboard input here (Use poke Tool)
endmodule

// REG
module REG_FILE (
  input  [15:0] BUS_IN,
  input  [2:0] DR,
  input  Clk,
  input  LD_REG,
  input  RESET,
  input  [2:0] SR2,
  input  [2:0] SR2_2,
  output [15:0] SR2_OUT,
  output [15:0] SR1_OUT
);

  wire decoder_1_out0, decoder_1_out1, decoder_1_out2, decoder_1_out3, decoder_1_out4, decoder_1_out5,
       decoder_1_out6, decoder_1_out7;
  wire [15:0] _0_q, _1_q, _2_q, _3_q, _4_q, _5_q, _6_q, _7_q;

  Decoder #(.select(3), .disabled(0)) decoder_1 (
    .out0(decoder_1_out0), .out1(decoder_1_out1), .out2(decoder_1_out2), .out3(decoder_1_out3),
    .out4(decoder_1_out4), .out5(decoder_1_out5), .out6(decoder_1_out6), .out7(decoder_1_out7), .sel(DR),
    .en(LD_REG));
  Register #(.width(16)) _0 (.D(BUS_IN), .en(decoder_1_out0), .Q(_0_q), .clk(Clk), .clr(RESET));
  Register #(.width(16)) _1 (.D(BUS_IN), .en(decoder_1_out1), .Q(_1_q), .clk(Clk), .clr(RESET));
  Multiplexer #(.select(3), .width(16), .enable("false")) multiplexer_1 (
    .in0(_0_q), .in1(_1_q), .in2(_2_q), .in3(_3_q), .in4(_4_q), .in5(_5_q), .in6(_6_q), .in7(_7_q),
    .out(SR2_OUT), .sel(SR2_2));
  Register #(.width(16)) _2 (.D(BUS_IN), .en(decoder_1_out2), .Q(_2_q), .clk(Clk), .clr(RESET));
  Register #(.width(16)) _3 (.D(BUS_IN), .en(decoder_1_out3), .Q(_3_q), .clk(Clk), .clr(RESET));
  Register #(.width(16)) _4 (.D(BUS_IN), .en(decoder_1_out4), .Q(_4_q), .clk(Clk), .clr(RESET));
  Register #(.width(16)) _5 (.D(BUS_IN), .en(decoder_1_out5), .Q(_5_q), .clk(Clk), .clr(RESET));
  Register #(.width(16)) _6 (.D(BUS_IN), .en(decoder_1_out6), .Q(_6_q), .clk(Clk), .clr(RESET));
  Multiplexer #(.select(3), .width(16), .enable("false")) multiplexer_2 (
    .in0(_0_q), .in1(_1_q), .in2(_2_q), .in3(_3_q), .in4(_4_q), .in5(_5_q), .in6(_6_q), .in7(_7_q),
    .out(SR1_OUT), .sel(SR2));
  Register #(.width(16)) _7 (.D(BUS_IN), .en(decoder_1_out7), .Q(_7_q), .clk(Clk), .clr(RESET));
endmodule

module PU (
  input  [15:0] BUS_IN,
  input  [2:0] DR,
  input  Clk,
  input  LD_REG,
  input  [2:0] SR1,
  input  [15:0] immeSEXT,
  input  [2:0] SR2,
  input  immeSelect,
  input  RESET,
  input  [1:0] ALUK,
  output [15:0] SR1OUT,
  output [15:0] ALU_TO_BUS
);

  wire [15:0] multiplexer_1_out, reg_file_1_sr2_out;

  Multiplexer #(.width(16), .enable("false")) multiplexer_1 (
    .in0(reg_file_1_sr2_out), .in1(immeSEXT), .out(multiplexer_1_out), .sel(immeSelect));
  Arith_and_Log_Unit ALU (.ALUK(ALUK), .SR2(multiplexer_1_out), .SR1(SR1OUT), .ALU_OUT(ALU_TO_BUS));
  REG_FILE reg_file_1 (
    .DR(DR), .LD_REG(LD_REG), .SR2_2(SR2), .RESET(RESET), .BUS_IN(BUS_IN), .Clk(Clk),
    .SR2_OUT(reg_file_1_sr2_out), .SR1_OUT(SR1OUT), .SR2(SR1));
endmodule

// ALU
module Arith_and_Log_Unit (
  input  [15:0] SR2,
  input  [15:0] SR1,
  input  [1:0] ALUK,
  output [15:0] ALU_OUT
);

  wire [15:0] adder_1_out, and_1_out, not_1_out;

  assign and_1_out = SR2 & SR1;  // AND_Gate and_1, 16 bits wide
  Multiplexer #(.select(2), .width(16)) multiplexer_1 (
    .in0(adder_1_out), .in1(and_1_out), .in2(not_1_out), .in3(SR1), .out(ALU_OUT), .sel(ALUK));  // open: en
  Adder #(.width(16)) adder_1 (.a(SR2), .b(SR1), .out(adder_1_out));  // open: cin, cout
  assign not_1_out = ~SR1;  // NOT_Gate not_1, 16 bits wide
endmodule

// MEM
module MEMORYIO (
  input  MIO_EN,
  input  R_W,
  input  [15:0] BUS,
  input  LD_MAR,
  input  LD_MDR,
  input  reset,
  input  Clk,
  input  KBSR,
  input  [6:0] KBDR,
  output [15:0] GateMDR,
  output [6:0] ASCII_OUT,
  output LD_DDR,
  output GOOUT,
  output GetChar
);

  wire address_control_logic_1_memen, GO, LDDSR, LDKBSR, not_1_out, not_2_out, or_1_out;
  wire [2:0] address_control_logic_1_inmux;
  wire [14:0] GO_REG_q;
  wire [15:0] controlled_buffer_2_out, MAR_q, multiplexer_1_out, multiplexer_2_out, ram_1_data;

  Register #(.width(16)) MAR (.D(BUS), .en(LD_MAR), .Q(MAR_q), .clk(Clk), .clr(reset));
  not not_1 (not_1_out, R_W);
  RAM #(.addrWidth(16), .dataWidth(16)) ram_1 (
    .addr(MAR_q), .data(ram_1_data), .sel(address_control_logic_1_memen), .clk(Clk), .ld(not_1_out));  // open: clr
  assign ram_1_data = R_W ? {GateMDR[15:7], ASCII_OUT} : 16'bz;  // Controlled_Buffer controlled_buffer_1
  or or_1 (or_1_out, reset, GO);
  Address_Control_Logic address_control_logic_1 (
    .MAR(MAR_q), .MIOEN(MIO_EN), .RW(R_W), .MEMEN(address_control_logic_1_memen),
    .INMUX(address_control_logic_1_inmux), .LDKBSR(LDKBSR), .LDDSR(LDDSR), .LDDDR(LD_DDR), .LStopClock(GO));
  assign controlled_buffer_2_out = GO ? {GateMDR[15:7], ASCII_OUT} : 16'bz;  // Controlled_Buffer controlled_buffer_2
  Multiplexer #(.select(3), .width(16), .enable("false")) multiplexer_1 (
    .in0(ram_1_data), .in1(16'h8000), .in2({KBSR, {15{1'b0}}}), .in3({{9{1'b0}}, KBDR}),
    .in4({GOOUT, GO_REG_q}), .out(multiplexer_1_out), .sel(address_control_logic_1_inmux));  // open: in5, in6, in7
  Register #(.width(16), .trigger("high")) GO_REG (
    .D(controlled_buffer_2_out), .en(or_1_out), .Q({GOOUT, GO_REG_q}), .clk(or_1_out));  // open: clr
  assign controlled_buffer_2_out = not_2_out ? {16{1'b1}} : 16'bz;  // Controlled_Buffer controlled_buffer_3
  not not_2 (not_2_out, GO);
  Multiplexer #(.width(16), .enable("false")) multiplexer_2 (
    .in0(BUS), .in1(multiplexer_1_out), .out(multiplexer_2_out), .sel(MIO_EN));
  Register #(.width(16)) MDR (
    .D(multiplexer_2_out), .en(LD_MDR), .Q({GateMDR[15:7], ASCII_OUT}), .clk(Clk), .clr(reset));
  and and_1 (GetChar, address_control_logic_1_inmux[1], address_control_logic_1_inmux[0]);

  assign GateMDR[6:0] = ASCII_OUT;

  // Other names for the same wires on the sheet: LDDDR = LD_DDR

  // Notes on the sheet:
  //   v Right Click to load program v
endmodule

module PCIR (
  input  [15:0] BUS_TO_PCMUX,
  input  MARMUX,
  input  LD_PC,
  input  [15:0] SR1_IN,
  input  [1:0] FINITE_TO_PCMUX,
  input  ADDR1MUX,
  input  RESET,
  input  [1:0] ADDR2MUX,
  input  LD_IR,
  input  [15:0] BUS_IN,
  input  Clk,
  output [15:0] GatePC,
  output [15:0] GateMARMUX,
  output [15:0] immOUT,
  output [15:0] TO_FSMC
);

  wire [9:0] multiplexer_3_out;
  wire [15:0] adder_1_out, adder_2_out, multiplexer_2_out, multiplexer_7_out, multiplexer_8_out;
  wire [15:9] multiplexer_4_out;
  wire [15:11] multiplexer_5_out;

  Multiplexer #(.width(16), .enable("false")) multiplexer_1 (
    .in0({{8{1'b0}}, TO_FSMC[7:5], immOUT[4:0]}), .in1(adder_1_out), .out(GateMARMUX), .sel(MARMUX));
  Multiplexer #(.select(2), .width(16), .enable("false")) multiplexer_2 (
    .in0({16{1'b0}}), .in1({multiplexer_3_out, TO_FSMC[5], immOUT[4:0]}),
    .in2({multiplexer_4_out, TO_FSMC[8:5], immOUT[4:0]}),
    .in3({multiplexer_5_out, TO_FSMC[10:5], immOUT[4:0]}), .out(multiplexer_2_out), .sel(ADDR2MUX));
  Multiplexer #(.width(10), .enable("false")) multiplexer_3 (
    .in0({10{1'b0}}), .in1({10{1'b1}}), .out(multiplexer_3_out), .sel(TO_FSMC[5]));
  Multiplexer #(.width(7), .enable("false")) multiplexer_4 (
    .in0({7{1'b0}}), .in1({7{1'b1}}), .out(multiplexer_4_out), .sel(TO_FSMC[8]));
  Register #(.width(16)) IR (.D(BUS_IN), .en(LD_IR), .Q({TO_FSMC[15:5], immOUT[4:0]}), .clk(Clk), .clr(RESET));
  Adder #(.width(16)) adder_1 (.a(multiplexer_8_out), .b(multiplexer_2_out), .out(adder_1_out));  // open: cin, cout
  Multiplexer #(.width(5), .enable("false")) multiplexer_5 (
    .in0({5{1'b0}}), .in1({5{1'b1}}), .out(multiplexer_5_out), .sel(TO_FSMC[10]));
  Multiplexer #(.width(11), .enable("false")) multiplexer_6 (
    .in0({11{1'b0}}), .in1({11{1'b1}}), .out(immOUT[15:5]), .sel(immOUT[4]));
  Register #(.width(16)) PC (.D(multiplexer_7_out), .en(LD_PC), .Q(GatePC), .clk(Clk), .clr(RESET));
  Multiplexer #(.select(2), .width(16), .enable("false")) multiplexer_7 (
    .in0(adder_2_out), .in1(BUS_TO_PCMUX), .in2(adder_1_out), .in3({16{1'b0}}), .out(multiplexer_7_out),
    .sel(FINITE_TO_PCMUX));
  Adder #(.width(16)) adder_2 (.a(GatePC), .b(16'h1), .out(adder_2_out));  // open: cin, cout
  Multiplexer #(.width(16), .enable("false")) multiplexer_8 (
    .in0(GatePC), .in1(SR1_IN), .out(multiplexer_8_out), .sel(ADDR1MUX));

  assign TO_FSMC[4:0] = immOUT[4:0];

  // Notes on the sheet:
  //   From left to right:
  //   [5:0] SEXT
  //   [8:0] SEXT
  //   [10:0] SEXT
  //   [4:0] SEXT to imm
endmodule

// NZP
module NZP_LOGIC (
  input  LD_CC,
  input  Clk,
  input  PSRMUX,
  input  [2:0] PSR_2_0,
  input  [15:0] NZP_LOGIC_IN,
  output [2:0] NZP_OUT
);

  wire or_1_out;
  wire [1:0] and_2_out;
  wire [2:0] multiplexer_1_out;

  and and_1 (and_2_out[1], ~and_2_out[0], ~NZP_LOGIC_IN[15]);  // AND_Gate
  Multiplexer #(.width(3), .enable("false")) multiplexer_1 (
    .in0({NZP_LOGIC_IN[15], and_2_out}), .in1(PSR_2_0), .out(multiplexer_1_out), .sel(PSRMUX));
  and and_2 (and_2_out[0], ~NZP_LOGIC_IN[15], or_1_out);  // AND_Gate
  or or_1 (or_1_out, NZP_LOGIC_IN[15], NZP_LOGIC_IN[14], NZP_LOGIC_IN[13], NZP_LOGIC_IN[12], NZP_LOGIC_IN[11], NZP_LOGIC_IN[10], NZP_LOGIC_IN[9], NZP_LOGIC_IN[8], NZP_LOGIC_IN[7], NZP_LOGIC_IN[6], NZP_LOGIC_IN[5], NZP_LOGIC_IN[4], NZP_LOGIC_IN[3], NZP_LOGIC_IN[2], NZP_LOGIC_IN[1], NZP_LOGIC_IN[0]);
  Register #(.width(3)) NZP (.D(multiplexer_1_out), .en(LD_CC), .Q(NZP_OUT), .clk(Clk));  // open: clr
endmodule

module FSM (
  input  Clk,
  input  R,
  input  PSR_15,
  input  INT,
  input  [15:0] IR,
  input  [2:0] NZP,
  input  RESET,
  output [19:0] LD_GATE_OUT,
  output [19:0] MUX_and_misc,
  output [2:0] DR_Select,
  output immSelect,
  output [2:0] SR1_Select,
  output [2:0] SR2_Select
);

  wire BEN_out;
  wire [1:0] register_1_q_2;
  wire [2:0] and_1_out, register_1_q_3;
  wire [5:0] bit_extender_1_out, microsequencer_1_select_out, multiplexer_1_out, register_1_q;
  wire [11:0] rom_1_data;
  wire [11:11] register_1_q_4;

  Register #(.width(16), .trigger("high")) IR_DEBUG (.D(IR), .en(1'b1), .clk(1'b1));  // open: Q, clr
  Microsequencer microsequencer_1 (
    .IR_11(IR[11]), .R(R), .BEN(BEN_out), .PSR_15(PSR_15), .INT(INT), .COND(register_1_q_3),
    .J(register_1_q), .Select_Out(microsequencer_1_select_out));
  assign bit_extender_1_out = {{2{1'b0}}, IR[15:12]};  // Bit_Extender bit_extender_1
  assign and_1_out = IR[11:9] & NZP;  // AND_Gate and_1, 3 bits wide
  or BEN (BEN_out, and_1_out[0], and_1_out[1], and_1_out[2]);
  Multiplexer #(.width(6), .enable("false")) multiplexer_1 (
    .in0(microsequencer_1_select_out), .in1(bit_extender_1_out), .out(multiplexer_1_out),
    .sel(register_1_q_4[11]));
  Multiplexer #(.select(2), .width(3), .enable("false")) multiplexer_2 (
    .in0(IR[11:9]), .in1(IR[8:6]), .in2(3'b110), .out(SR1_Select), .sel(MUX_and_misc[15:14]));  // open: in3
  ROM #(.addrWidth(6), .dataWidth(12)) rom_1 (.addr(multiplexer_1_out), .data(rom_1_data), .sel(1'b1));
  ROM #(.addrWidth(6), .dataWidth(20)) rom_2 (.addr(multiplexer_1_out), .data(LD_GATE_OUT), .sel(1'b1));
  ROM #(.addrWidth(6), .dataWidth(20)) rom_3 (.addr(multiplexer_1_out), .data(MUX_and_misc), .sel(1'b1));
  Multiplexer #(.select(2), .width(3), .enable("false")) multiplexer_3 (
    .in0(IR[11:9]), .in1(3'b111), .in2(3'b110), .out(DR_Select), .sel(MUX_and_misc[17:16]));  // open: in3
  Register #(.width(12), .trigger("falling")) register_1 (
    .D(rom_1_data), .Q({register_1_q_4[11], register_1_q_3, register_1_q_2, register_1_q}), .clk(Clk),
    .clr(RESET));  // open: en

  assign immSelect = IR[5];
  assign SR2_Select = IR[2:0];

  // Other names for the same wires on the sheet: SR1[1:0] = MUX_and_misc[15:14]; DR[1:0] = MUX_and_misc[17:16]

  // Notes on the sheet:
  //   IRD,COND,J
  //   LD and Gate Signals
  //   Mux, memory and priorety signals
  //   contents of rom_1 (hex, n*v repeats v):
  //   212 12 19 17 314 12 19 17 424 12 18 1d 12 625 12 1c 110 3f 521 3f 12 12 12 10 118 119 19 12 11c 11d
  //   12 17 800 121 433 20 124 29 27 28 128 129 22 2f 2d 25 3f 30 130 425 34 12 134 3f 12 4*3f 12 4*3f
  //   contents of rom_2 (hex, n*v repeats v):
  //   0 6020 40010 40010 0 6020 40010 40010 40020 6020 40010 40010 1000 20902 6010 40010 0 ff 41080 ff
  //   5080 5080 1000 20020 20000 20000 40040 6040 24080 20000 1040 40040 8000 20000 4001 10040 20000 44001
  //   1040 44001 40000 0 2840 20004 20902 4201 ff 44001 0 a0902 40008 0 20000 ff 1040 4*ff 4401 4*ff
  //   contents of rom_3 (hex, n*v repeats v):
  //   0 4000 1100 1100 0 4008 6900 6900 8018 4010 1100 1100 86000 81 1100 0 6 ffff8 0 ffff8 96000 91800
  //   81000 18 4 4 0 0 10004 4 40000 0 0 4 28000 0 4 28200 40000 28000 4 6 20 0 41 28400 ffff8 28200 6 1 0
  //   0 4 ffff8 40000 4*ffff8 28600 4*ffff8
endmodule

// MicroS
module Microsequencer (
  input  IR_11,
  input  R,
  input  BEN,
  input  PSR_15,
  input  INT,
  input  [2:0] COND,
  input  [5:0] J,
  output [5:0] Select_Out
);

  wire Addr__md_out, Branch_out, Int_Prsnt_out, Ready_out, UPM_out;

  and Addr__md (Addr__md_out, IR_11, COND[0], COND[1], ~COND[2]);  // AND_Gate
  and Ready (Ready_out, R, COND[0], ~COND[1], ~COND[2]);  // AND_Gate
  and Branch (Branch_out, BEN, ~COND[0], COND[1], ~COND[2]);  // AND_Gate
  and UPM (UPM_out, PSR_15, ~COND[0], ~COND[1], COND[2]);  // AND_Gate
  and Int_Prsnt (Int_Prsnt_out, INT, COND[0], ~COND[1], COND[2]);  // AND_Gate
  or or_1 (Select_Out[0], Addr__md_out, J[0]);
  or or_2 (Select_Out[1], Ready_out, J[1]);
  or or_3 (Select_Out[2], Branch_out, J[2]);
  or or_4 (Select_Out[3], UPM_out, J[3]);
  or or_5 (Select_Out[4], Int_Prsnt_out, J[4]);

  assign Select_Out[5] = J[5];
endmodule

module SP_logic (
  input  [15:0] SR1IN,
  input  LD_SavedUSP,
  input  LD_SavedSSP,
  input  [1:0] SPMUX,
  output [15:0] GateSP
);

  wire [15:0] register_1_q, register_2_q, undriven, undriven_2;

  Register #(.width(16)) register_1 (.D(SR1IN), .en(LD_SavedUSP), .Q(register_1_q));  // open: clk, clr
  Adder #(.width(16)) adder_1 (.a(SR1IN), .b(16'h1));  // open: out, cin, cout
  Subtractor #(.width(16)) subtractor_1 (.a(SR1IN), .b(16'h1));  // open: out, bin, bout
  Register #(.width(16)) register_2 (.D(SR1IN), .en(LD_SavedSSP), .Q(register_2_q));  // open: clk, clr
  Multiplexer #(.select(2), .width(16), .enable("false")) multiplexer_1 (
    .in0(undriven), .in1(undriven_2), .in2(register_2_q), .in3(register_1_q), .out(GateSP), .sel(SPMUX));
endmodule

// INT
module Priorety_INT (
  input  LD_Priv,
  input  Clk,
  input  PSRMux,
  input  [2:0] BUS_10_8,
  input  [2:0] To_BUS__10_8,
  output INT
);

  wire [2:0] multiplexer_1_out;

  Register #(.width(3), .trigger("falling")) register_1 (
    .D(multiplexer_1_out), .en(LD_Priv), .Q(To_BUS__10_8), .clk(Clk));  // open: clr
  Multiplexer #(.width(3), .enable("false")) multiplexer_1 (
    .in0(3'b000), .in1(BUS_10_8), .out(multiplexer_1_out), .sel(PSRMux));
  Comparator #(.width(3), .mode("unsigned")) comparator_1 (.a(3'b000), .b(To_BUS__10_8), .gt(INT));  // open: eq, lt
endmodule

// MemLog
module Address_Control_Logic (
  input  [15:0] MAR,
  input  MIOEN,
  input  RW,
  output MEMEN,
  output [2:0] INMUX,
  output LDKBSR,
  output LDDSR,
  output LDDDR,
  output LStopClock
);

  wire and_1_out, and_2_out, and_3_out, and_4_out, comparator_1_eq, comparator_2_eq, comparator_3_eq,
       comparator_4_eq, comparator_5_eq;

  Comparator #(.width(16), .mode("unsigned")) comparator_1 (
    .a(MAR), .b(16'hfe00), .eq(comparator_1_eq));  // open: gt, lt
  Comparator #(.width(16), .mode("unsigned")) comparator_2 (
    .a(MAR), .b(16'hfe02), .eq(comparator_2_eq));  // open: gt, lt
  Comparator #(.width(16), .mode("unsigned")) comparator_3 (
    .a(MAR), .b(16'hfe04), .eq(comparator_3_eq));  // open: gt, lt
  Comparator #(.width(16), .mode("unsigned")) comparator_4 (
    .a(MAR), .b(16'hfe06), .eq(comparator_4_eq));  // open: gt, lt
  Comparator #(.width(16), .mode("unsigned")) comparator_5 (
    .a(MAR), .b(16'hfffe), .eq(comparator_5_eq));  // open: gt, lt
  nor nor_1 (MEMEN, comparator_1_eq, comparator_2_eq, comparator_3_eq, comparator_4_eq, comparator_5_eq, ~MIOEN);  // NOR_Gate
  and and_1 (and_1_out, comparator_2_eq, MIOEN, ~RW);  // AND_Gate
  or or_1 (INMUX[0], and_1_out, and_2_out);
  and and_2 (and_2_out, comparator_3_eq, MIOEN, ~RW);  // AND_Gate
  and and_3 (and_3_out, comparator_1_eq, MIOEN, ~RW);  // AND_Gate
  or or_2 (INMUX[1], and_3_out, and_4_out);
  and and_4 (and_4_out, comparator_2_eq, MIOEN, ~RW);  // AND_Gate
  and and_5 (INMUX[2], comparator_5_eq, MIOEN, ~RW);  // AND_Gate
  and and_6 (LDKBSR, comparator_1_eq, MIOEN, RW);
  and and_7 (LDDSR, comparator_3_eq, MIOEN, RW);
  and and_8 (LDDDR, comparator_4_eq, MIOEN, RW);
  and and_9 (LStopClock, comparator_5_eq, MIOEN, RW);
endmodule

module Vector (
  input  [1:0] VectorMUX,
  input  [7:0] INTV,
  output [15:0] GateVector
);

  Multiplexer #(.select(2), .width(8), .enable("false")) multiplexer_1 (
    .in0(INTV), .in1({8{1'b0}}), .in2(8'h1), .out(GateVector[7:0]), .sel(VectorMUX));  // open: in3

  assign GateVector[15:8] = 8'h1;
endmodule
