// Logisim project LC3-2-0.circ as structural Verilog: 10 circuits, main circuit main
module main (
  input  RESET
);

  wire ADDR1M, ALUG, Clock, CLOCK_out, GetChar, GO, immSel, KBSR, LCC, Load_Disp, MARM, MIO_EN;
  wire [1:0] ADDR2M, ALUM, DRM;
  wire [2:0] DRSel, nzp_logic_1_nzp_out, SR1Sel, SR2Sel;
  wire [6:0] Display, KBDR;
  wire [12:1] LDGATE;
  wire [13:0] MUX_IO;
  wire [15:0] BUS, MBUS, memoryio_1_gatemem, memoryio_1_memgatemar, pcir_1_gatemarmux, pcir_1_gatepc,
       pcir_1_immout, pcir_1_memgatemarmux, pcir_1_memgatepc, pcir_1_pc_debug, pcir_1_to_fsmc,
       pu_1_alu_to_bus, pu_1_sr1out;

  Clock u_CLOCK (.out(CLOCK_out));
  and and_1 (Clock, CLOCK_out, GO);
  TTY #(.rows(30), .cols(85)) tty_1 (.data(Display), .clk(Clock), .we(Load_Disp), .clr(RESET));
  Keyboard keyboard_1 (.clk(Clock), .re(GetChar), .clr(RESET), .avail(KBSR), .data(KBDR));
  assign BUS = LDGATE[1] ? pcir_1_gatemarmux : 16'bz;  // Controlled_Buffer controlled_buffer_1
  NZP_LOGIC nzp_logic_1 (.LD_CC(LCC), .Clk(Clock), .NZP_OUT(nzp_logic_1_nzp_out), .NZP_LOGIC_IN(BUS));
  assign MBUS = LDGATE[4] ? pcir_1_memgatepc : 16'bz;  // Controlled_Buffer controlled_buffer_2
  assign MBUS = LDGATE[5] ? pcir_1_memgatemarmux : 16'bz;  // Controlled_Buffer controlled_buffer_3
  assign BUS = LDGATE[2] ? pcir_1_gatepc : 16'bz;  // Controlled_Buffer controlled_buffer_4
  FSM fsm_1 (
    .IR(pcir_1_to_fsmc), .NZP(nzp_logic_1_nzp_out), .LD_GATE_OUT({LDGATE[12:10], LCC, LDGATE[8:1], ALUG}),
    .MUX_and_misc({MUX_IO[13:12], DRM, MUX_IO[9:8], ADDR1M, ADDR2M, MARM, ALUM, MIO_EN, MUX_IO[0]}),
    .DR_Select(DRSel), .SR1_Select(SR1Sel), .SR2_Select(SR2Sel), .Clk(Clock), .immSelect(immSel),
    .RESET(RESET), .PC_DEBUG(pcir_1_pc_debug));
  PCIR pcir_1 (
    .LD_PC(LDGATE[8]), .FINITE_TO_PCMUX(MUX_IO[13:12]), .ADDR2MUX(ADDR2M), .LD_IR(LDGATE[11]), .Clk(Clock),
    .SR1_IN(pu_1_sr1out), .immOUT(pcir_1_immout), .TO_FSMC(pcir_1_to_fsmc), .BUS_TO_PCMUX(BUS),
    .GatePC(pcir_1_gatepc), .BUS_IN(BUS), .MARMUX(MARM), .GateMARMUX(pcir_1_gatemarmux), .ADDR1MUX(ADDR1M),
    .RESET(RESET), .MEMGatePC(pcir_1_memgatepc), .MEMGateMARMUX(pcir_1_memgatemarmux),
    .PC_DEBUG(pcir_1_pc_debug));
  assign BUS = ALUG ? pu_1_alu_to_bus : 16'bz;  // Controlled_Buffer controlled_buffer_5
  MEMORYIO memoryio_1 (
    .LD_MAR(LDGATE[12]), .Clk(Clock), .MemGateMAR(memoryio_1_memgatemar), .reset(RESET), .BUS(BUS),
    .MIO_EN(MIO_EN), .R_W(MUX_IO[0]), .GOOUT(GO), .ASCII_OUT(Display), .LD_DDR(Load_Disp), .GetChar(GetChar),
    .KBSR(KBSR), .KBDR(KBDR), .MemBUS(MBUS), .GateMEM(memoryio_1_gatemem));
  PU pu_1 (
    .DR(DRSel), .LD_REG(LDGATE[10]), .SR2(SR2Sel), .immeSelect(immSel), .ALUK(ALUM), .SR1(SR1Sel),
    .immeSEXT(pcir_1_immout), .BUS_IN(BUS), .Clk(Clock), .ALU_TO_BUS(pu_1_alu_to_bus), .SR1OUT(pu_1_sr1out),
    .RESET(RESET));
  assign BUS = LDGATE[3] ? memoryio_1_gatemem : 16'bz;  // Controlled_Buffer controlled_buffer_6
  assign MBUS = LDGATE[6] ? memoryio_1_memgatemar : 16'bz;  // Controlled_Buffer controlled_buffer_7

  // Other names for the same wires on the sheet: LDGATE (some bits) = {LCC, ALUG}; MARG = LDGATE[1]; PCG = LDGATE[2];
  //   MemG = LDGATE[3]; PCMG = LDGATE[4]; MARMMG = LDGATE[5]; MARMG = LDGATE[6]; LPC = LDGATE[8]; LREG = LDGATE[10];
  //   LIR = LDGATE[11]; LMAR = LDGATE[12]; R_W = MUX_IO[0];
  //   MUX_IO (some bits) = {DRM, ADDR1M, ADDR2M, MARM, ALUM, MIO_EN}; SR1M[1:0] = MUX_IO[9:8];
  //   PCM[1:0] = MUX_IO[13:12]

  // Notes on the sheet:
  //   Keyboard input here (Use poke Tool)
endmodule

// Processing Unit
module PU (
  input  [15:0] BUS_IN,
  input  [2:0] DR,
  input  Clk,
  input  LD_REG,
  input  [2:0] SR1,
  input  [15:0] immeSEXT,
  input  [2:0] SR2,
  input  immeSelect,
  input  RESET,
  input  [1:0] ALUK,
  output [15:0] SR1OUT,
  output [15:0] ALU_TO_BUS
);

  wire [15:0] multiplexer_1_out, reg_file_1_sr2_out;

  Multiplexer #(.width(16), .enable("false")) multiplexer_1 (
    .in0(reg_file_1_sr2_out), .in1(immeSEXT), .out(multiplexer_1_out), .sel(immeSelect));
  Arith_and_Log_Unit ALU (.ALUK(ALUK), .SR2(multiplexer_1_out), .SR1(SR1OUT), .ALU_OUT(ALU_TO_BUS));
  Reg_File reg_file_1 (
    .DR(DR), .LD_REG(LD_REG), .SR2_2(SR2), .RESET(RESET), .BUS_IN(BUS_IN), .Clk(Clk),
    .SR2_OUT(reg_file_1_sr2_out), .SR1_OUT(SR1OUT), .SR2(SR1));
endmodule

// Main Memory
module MEMORYIO (
  input  MIO_EN,
  input  R_W,
  input  [15:0] BUS,
  input  [15:0] MemBUS,
  input  LD_MAR,
  input  reset,
  input  Clk,
  input  KBSR,
  input  [6:0] KBDR,
  output [15:0] GateMEM,
  output [15:0] MemGateMAR,
  output [6:0] ASCII_OUT,
  output LD_DDR,
  output GOOUT,
  output GetChar
);

  wire address_control_logic_1_memen, GO, LDDSR, LDKBSR, not_1_out, not_2_out, or_1_out;
  wire [2:0] address_control_logic_1_inmux;
  wire [14:0] GO_REG_q;
  wire [15:0] controlled_buffer_2_out, ram_1_data;

  not not_1 (not_1_out, R_W);
  RAM #(.addrWidth(16), .dataWidth(16)) ram_1 (
    .addr(MemBUS), .data(ram_1_data), .sel(address_control_logic_1_memen), .clk(Clk), .ld(not_1_out));  // open: clr
  assign ram_1_data = R_W ? BUS : 16'bz;  // Controlled_Buffer controlled_buffer_1
  or or_1 (or_1_out, reset, GO);
  Address_Control_Logic address_control_logic_1 (
    .MAR(MemBUS), .MIOEN(MIO_EN), .RW(R_W), .MEMEN(address_control_logic_1_memen),
    .INMUX(address_control_logic_1_inmux), .LDKBSR(LDKBSR), .LDDSR(LDDSR), .LDDDR(LD_DDR), .LStopClock(GO));
  assign controlled_buffer_2_out = GO ? BUS : 16'bz;  // Controlled_Buffer controlled_buffer_2
  Multiplexer #(.select(3), .width(16), .enable("false")) multiplexer_1 (
    .in0(ram_1_data), .in1(16'h8000), .in2({KBSR, {15{1'b0}}}), .in3({{9{1'b0}}, KBDR}),
    .in4({GOOUT, GO_REG_q}), .in7(MemBUS), .out(GateMEM), .sel(address_control_logic_1_inmux));  // open: in5, in6
  Register #(.width(16), .trigger("high")) GO_REG (
    .D(controlled_buffer_2_out), .en(or_1_out), .Q({GOOUT, GO_REG_q}), .clk(or_1_out));  // open: clr
  assign controlled_buffer_2_out = not_2_out ? {16{1'b1}} : 16'bz;  // Controlled_Buffer controlled_buffer_3
  not not_2 (not_2_out, GO);
  Register #(.width(16)) MAR (.D(GateMEM), .en(LD_MAR), .Q(MemGateMAR), .clk(Clk), .clr(reset));
  and and_1 (GetChar, address_control_logic_1_inmux[1], address_control_logic_1_inmux[0]);

  assign ASCII_OUT = BUS[6:0];

  // Other names for the same wires on the sheet: LDDDR = LD_DDR; MBUS[15:0] = MemBUS

  // Notes on the sheet:
  //   v Right Click to load program v
endmodule

// Information Unit
module PCIR (
  input  [15:0] BUS_TO_PCMUX,
  input  MARMUX,
  input  LD_PC,
  input  [15:0] SR1_IN,
  input  [1:0] FINITE_TO_PCMUX,
  input  ADDR1MUX,
  input  RESET,
  input  [1:0] ADDR2MUX,
  input  LD_IR,
  input  [15:0] BUS_IN,
  input  Clk,
  output [15:0] GatePC,
  output [15:0] MEMGatePC,
  output [15:0] GateMARMUX,
  output [15:0] PC_DEBUG,
  output [15:0] MEMGateMARMUX,
  output [15:0] immOUT,
  output [15:0] TO_FSMC
);

  wire [9:0] multiplexer_3_out;
  wire [15:0] adder_1_out, adder_2_out, multiplexer_2_out, multiplexer_7_out, multiplexer_8_out;
  wire [15:9] multiplexer_4_out;
  wire [15:11] multiplexer_5_out;

  Multiplexer #(.width(16), .enable("false")) multiplexer_1 (
    .in0({{8{1'b0}}, TO_FSMC[7:5], immOUT[4:0]}), .in1(adder_1_out), .out(GateMARMUX), .sel(MARMUX));
  Multiplexer #(.select(2), .width(16), .enable("false")) multiplexer_2 (
    .in0({16{1'b0}}), .in1({multiplexer_3_out, TO_FSMC[5], immOUT[4:0]}),
    .in2({multiplexer_4_out, TO_FSMC[8:5], immOUT[4:0]}),
    .in3({multiplexer_5_out, TO_FSMC[10:5], immOUT[4:0]}), .out(multiplexer_2_out), .sel(ADDR2MUX));
  Multiplexer #(.width(10), .enable("false")) multiplexer_3 (
    .in0({10{1'b0}}), .in1({10{1'b1}}), .out(multiplexer_3_out), .sel(TO_FSMC[5]));
  Multiplexer #(.width(7), .enable("false")) multiplexer_4 (
    .in0({7{1'b0}}), .in1({7{1'b1}}), .out(multiplexer_4_out), .sel(TO_FSMC[8]));
  Register #(.width(16)) IR (.D(BUS_IN), .en(LD_IR), .Q({TO_FSMC[15:5], immOUT[4:0]}), .clk(Clk), .clr(RESET));
  Adder #(.width(16)) adder_1 (.a(multiplexer_8_out), .b(multiplexer_2_out), .out(adder_1_out));  // open: cin, cout
  Multiplexer #(.width(5), .enable("false")) multiplexer_5 (
    .in0({5{1'b0}}), .in1({5{1'b1}}), .out(multiplexer_5_out), .sel(TO_FSMC[10]));
  Multiplexer #(.width(11), .enable("false")) multiplexer_6 (
    .in0({11{1'b0}}), .in1({11{1'b1}}), .out(immOUT[15:5]), .sel(immOUT[4]));
  Register #(.width(16)) PC (.D(multiplexer_7_out), .en(LD_PC), .Q(GatePC), .clk(Clk), .clr(RESET));
  Multiplexer #(.select(2), .width(16), .enable("false")) multiplexer_7 (
    .in0(adder_2_out), .in1(BUS_TO_PCMUX), .in2(adder_1_out), .in3({16{1'b0}}), .out(multiplexer_7_out),
    .sel(FINITE_TO_PCMUX));
  Adder #(.width(16)) adder_2 (.a(GatePC), .b(16'h1), .out(adder_2_out));  // open: cin, cout
  Multiplexer #(.width(16), .enable("false")) multiplexer_8 (
    .in0(GatePC), .in1(SR1_IN), .out(multiplexer_8_out), .sel(ADDR1MUX));

  assign MEMGateMARMUX = GateMARMUX;
  assign MEMGatePC = GatePC;
  assign PC_DEBUG = GatePC;
  assign TO_FSMC[4:0] = immOUT[4:0];

  // Notes on the sheet:
  //   From left to right:
  //   [5:0] SEXT
  //   [8:0] SEXT
  //   [10:0] SEXT
  //   [4:0] SEXT to imm
endmodule

// NZP Logic Unit
module NZP_LOGIC (
  input  LD_CC,
  input  Clk,
  input  [15:0] NZP_LOGIC_IN,
  output [2:0] NZP_OUT
);

  wire or_1_out;
  wire [1:0] and_2_out;

  and and_1 (and_2_out[1], ~and_2_out[0], ~NZP_LOGIC_IN[15]);  // AND_Gate
  and and_2 (and_2_out[0], ~NZP_LOGIC_IN[15], or_1_out);  // AND_Gate
  or or_1 (or_1_out, NZP_LOGIC_IN[15], NZP_LOGIC_IN[14], NZP_LOGIC_IN[13], NZP_LOGIC_IN[12], NZP_LOGIC_IN[11], NZP_LOGIC_IN[10], NZP_LOGIC_IN[9], NZP_LOGIC_IN[8], NZP_LOGIC_IN[7], NZP_LOGIC_IN[6], NZP_LOGIC_IN[5], NZP_LOGIC_IN[4], NZP_LOGIC_IN[3], NZP_LOGIC_IN[2], NZP_LOGIC_IN[1], NZP_LOGIC_IN[0]);
  Register #(.width(3)) NZP (.D({NZP_LOGIC_IN[15], and_2_out}), .en(LD_CC), .Q(NZP_OUT), .clk(Clk));  // open: clr
endmodule

// Control Unit
module FSM (
  input  [15:0] PC_DEBUG,
  input  Clk,
  input  [15:0] IR,
  input  [2:0] NZP,
  input  RESET,
  output [12:0] LD_GATE_OUT,
  output [13:0] MUX_and_misc,
  output [2:0] DR_Select,
  output immSelect,
  output [2:0] SR1_Select,
  output [2:0] SR2_Select
);

  wire BEN_out;
  wire [1:0] register_1_q_3;
  wire [2:0] and_1_out;
  wire [4:0] bit_extender_1_out, microsequencer_1_select_out, multiplexer_1_out, register_1_q;
  wire [10:0] rom_1_data;
  wire [10:5] register_1_q_2;

  Microsequencer microsequencer_1 (
    .IR_11(IR[11]), .BEN(BEN_out), .COND(register_1_q_3), .J(register_1_q),
    .Select_Out(microsequencer_1_select_out));
  assign bit_extender_1_out = {{1{1'b0}}, IR[15:12]};  // Bit_Extender bit_extender_1
  assign and_1_out = IR[11:9] & NZP;  // AND_Gate and_1, 3 bits wide
  or BEN (BEN_out, and_1_out[0], and_1_out[1], and_1_out[2]);
  Multiplexer #(.width(5), .enable("false")) multiplexer_1 (
    .in0(microsequencer_1_select_out), .in1(bit_extender_1_out), .out(multiplexer_1_out),
    .sel(register_1_q_2[10]));
  Multiplexer #(.select(2), .width(3), .enable("false")) multiplexer_2 (
    .in0(IR[11:9]), .in1(IR[8:6]), .in2(3'b110), .out(SR1_Select), .sel(MUX_and_misc[9:8]));  // open: in3
  ROM #(.addrWidth(5), .dataWidth(11)) rom_1 (.addr(multiplexer_1_out), .data(rom_1_data), .sel(1'b1));
  ROM #(.addrWidth(5), .dataWidth(13)) rom_2 (.addr(multiplexer_1_out), .data(LD_GATE_OUT), .sel(1'b1));
  ROM #(.addrWidth(5), .dataWidth(14)) rom_3 (.addr(multiplexer_1_out), .data(MUX_and_misc), .sel(1'b1));
  Multiplexer #(.select(2), .width(3), .enable("false")) multiplexer_3 (
    .in0(IR[11:9]), .in1(3'b111), .in2(3'b110), .out(DR_Select), .sel(MUX_and_misc[11:10]));  // open: in3
  Register #(.width(11), .trigger("falling")) register_1 (
    .D(rom_1_data), .Q({register_1_q_2[10], register_1_q_3, register_1_q_2[7:5], register_1_q}), .clk(Clk),
    .clr(RESET));  // open: en
  Register #(.width(16), .trigger("high")) IR_DEBUG (.D(IR), .en(1'b1), .clk(1'b1));  // open: Q, clr
  Register #(.width(16), .trigger("high")) u_PC_DEBUG (.D(PC_DEBUG), .en(1'b1), .clk(1'b1));  // open: Q, clr

  assign immSelect = IR[5];
  assign SR2_Select = IR[2:0];

  // Other names for the same wires on the sheet: LD_BEN = LD_GATE_OUT[7]; SR1[1:0] = MUX_and_misc[9:8];
  //   DR[1:0] = MUX_and_misc[11:10]

  // Notes on the sheet:
  //   IRD,COND,J
  //   LD and Gate Signals
  //   Mux, memory and priorety signals
  //   contents of rom_1 (hex, n*v repeats v):
  //   110 10 10 10 21c 10 10 14 1f 10 13 14 10 1f 10 11 400 4*10 7*1f 10 10 1f 1f
  //   contents of rom_2 (hex, n*v repeats v):
  //   0 601 628 21 0 601 628 1020 0 601 1020 1020 101 0 402 404 998 128 100 648 41 7*0 504 504
  //   contents of rom_3 (hex, n*v repeats v):
  //   0 100 52 5f 0 104 1b2 1b2 0 108 52 52 2180 0 50 400 2 1002 2040 2 f 7*0 2580 2460
endmodule

// REG
module Reg_File (
  input  [15:0] BUS_IN,
  input  [2:0] DR,
  input  Clk,
  input  LD_REG,
  input  RESET,
  input  [2:0] SR2,
  input  [2:0] SR2_2,
  output [15:0] SR2_OUT,
  output [15:0] SR1_OUT
);

  wire decoder_1_out0, decoder_1_out1, decoder_1_out2, decoder_1_out3, decoder_1_out4, decoder_1_out5,
       decoder_1_out6, decoder_1_out7;
  wire [15:0] _0_q, _1_q, _2_q, _3_q, _4_q, _5_q, _6_q, _7_q;

  Decoder #(.select(3), .disabled(0)) decoder_1 (
    .out0(decoder_1_out0), .out1(decoder_1_out1), .out2(decoder_1_out2), .out3(decoder_1_out3),
    .out4(decoder_1_out4), .out5(decoder_1_out5), .out6(decoder_1_out6), .out7(decoder_1_out7), .sel(DR),
    .en(LD_REG));
  Register #(.width(16)) _0 (.D(BUS_IN), .en(decoder_1_out0), .Q(_0_q), .clk(Clk), .clr(RESET));
  Register #(.width(16)) _1 (.D(BUS_IN), .en(decoder_1_out1), .Q(_1_q), .clk(Clk), .clr(RESET));
  Multiplexer #(.select(3), .width(16), .enable("false")) multiplexer_1 (
    .in0(_0_q), .in1(_1_q), .in2(_2_q), .in3(_3_q), .in4(_4_q), .in5(_5_q), .in6(_6_q), .in7(_7_q),
    .out(SR2_OUT), .sel(SR2_2));
  Register #(.width(16)) _2 (.D(BUS_IN), .en(decoder_1_out2), .Q(_2_q), .clk(Clk), .clr(RESET));
  Register #(.width(16)) _3 (.D(BUS_IN), .en(decoder_1_out3), .Q(_3_q), .clk(Clk), .clr(RESET));
  Register #(.width(16)) _4 (.D(BUS_IN), .en(decoder_1_out4), .Q(_4_q), .clk(Clk), .clr(RESET));
  Register #(.width(16)) _5 (.D(BUS_IN), .en(decoder_1_out5), .Q(_5_q), .clk(Clk), .clr(RESET));
  Register #(.width(16)) _6 (.D(BUS_IN), .en(decoder_1_out6), .Q(_6_q), .clk(Clk), .clr(RESET));
  Multiplexer #(.select(3), .width(16), .enable("false")) multiplexer_2 (
    .in0(_0_q), .in1(_1_q), .in2(_2_q), .in3(_3_q), .in4(_4_q), .in5(_5_q), .in6(_6_q), .in7(_7_q),
    .out(SR1_OUT), .sel(SR2));
  Register #(.width(16)) _7 (.D(BUS_IN), .en(decoder_1_out7), .Q(_7_q), .clk(Clk), .clr(RESET));
endmodule

// ALU
module Arith_and_Log_Unit (
  input  [15:0] SR2,
  input  [15:0] SR1,
  input  [1:0] ALUK,
  output [15:0] ALU_OUT
);

  wire [15:0] adder_1_out, and_1_out, not_1_out;

  assign and_1_out = SR2 & SR1;  // AND_Gate and_1, 16 bits wide
  Multiplexer #(.select(2), .width(16)) multiplexer_1 (
    .in0(adder_1_out), .in1(and_1_out), .in2(not_1_out), .in3(SR1), .out(ALU_OUT), .sel(ALUK));  // open: en
  Adder #(.width(16)) adder_1 (.a(SR2), .b(SR1), .out(adder_1_out));  // open: cin, cout
  assign not_1_out = ~SR1;  // NOT_Gate not_1, 16 bits wide
endmodule

// MicroS
module Microsequencer (
  input  IR_11,
  input  BEN,
  input  [1:0] COND,
  input  [4:0] J,
  output [4:0] Select_Out
);

  wire Addr__md_out, Branch_out;

  and Addr__md (Addr__md_out, IR_11, COND[1], ~COND[0]);  // AND_Gate
  and Branch (Branch_out, BEN, ~COND[1], COND[0]);  // AND_Gate
  or or_1 (Select_Out[0], Addr__md_out, J[0]);
  or or_2 (Select_Out[1], Branch_out, J[1]);

  assign Select_Out[4:2] = J[4:2];
endmodule

// MemLog
module Address_Control_Logic (
  input  [15:0] MAR,
  input  MIOEN,
  input  RW,
  output MEMEN,
  output [2:0] INMUX,
  output LDKBSR,
  output LDDSR,
  output LDDDR,
  output LStopClock
);

  wire and_1_out, and_2_out, and_3_out, and_4_out, and_5_out, and_6_out, comparator_1_eq, comparator_2_eq,
       comparator_3_eq, comparator_4_eq, comparator_5_eq;

  Comparator #(.width(16), .mode("unsigned")) comparator_1 (
    .a(MAR), .b(16'hfe00), .eq(comparator_1_eq));  // open: gt, lt
  Comparator #(.width(16), .mode("unsigned")) comparator_2 (
    .a(MAR), .b(16'hfe02), .eq(comparator_2_eq));  // open: gt, lt
  Comparator #(.width(16), .mode("unsigned")) comparator_3 (
    .a(MAR), .b(16'hfe04), .eq(comparator_3_eq));  // open: gt, lt
  Comparator #(.width(16), .mode("unsigned")) comparator_4 (
    .a(MAR), .b(16'hfe06), .eq(comparator_4_eq));  // open: gt, lt
  Comparator #(.width(16), .mode("unsigned")) comparator_5 (
    .a(MAR), .b(16'hfffe), .eq(comparator_5_eq));  // open: gt, lt
  nor nor_1 (MEMEN, comparator_1_eq, comparator_2_eq, comparator_3_eq, comparator_4_eq, comparator_5_eq, ~MIOEN);  // NOR_Gate
  and and_1 (and_1_out, comparator_2_eq, MIOEN, ~RW);  // AND_Gate
  or or_1 (INMUX[0], and_1_out, and_6_out, and_2_out);
  and and_2 (and_2_out, comparator_3_eq, MIOEN, ~RW);  // AND_Gate
  and and_3 (and_3_out, comparator_1_eq, MIOEN, ~RW);  // AND_Gate
  or or_2 (INMUX[1], and_3_out, and_6_out, and_4_out);
  and and_4 (and_4_out, comparator_2_eq, MIOEN, ~RW);  // AND_Gate
  and and_5 (and_5_out, comparator_5_eq, MIOEN, ~RW);  // AND_Gate
  or or_3 (INMUX[2], and_5_out, and_6_out);
  and and_6 (and_6_out, RW, ~MIOEN);  // AND_Gate
  and and_7 (LDKBSR, comparator_1_eq, MIOEN, RW);
  and and_8 (LDDSR, comparator_3_eq, MIOEN, RW);
  and and_9 (LDDDR, comparator_4_eq, MIOEN, RW);
  and and_10 (LStopClock, comparator_5_eq, MIOEN, RW);
endmodule
